# Fritzing sketch no-pcb (saved by Fritzing 0.9.3b)

parts:
  Pusher_Motor = DC Motor  # not connected
  CPU = Arduino Nano (Rev3.0)
  Auto_Switch = Taiway 100-SP-X-T1 SPDT Miniature Toggle Switch [part_number=100-SP-X-T1-0-0-B1-M1 package=THT]
  Trigger_Switch = Taiway 100-SP-X-T1 SPDT Miniature Toggle Switch [part_number=100-SP-X-T1-0-0-B1-M1 package=THT]
  Disconnector_Switch = Taiway 100-SP-X-T1 SPDT Miniature Toggle Switch [part_number=100-SP-X-T1-0-0-B1-M1 package=THT]
  100k = Resistor [tolerance=±5% resistance=100k package=THT]
  1M = Resistor [tolerance=±5% resistance=1M package=THT]
  4_7k = Resistor [tolerance=±5% resistance=4.7 package=THT]
  Battery = Battery block 9V

nets:
  N1: CPU.GND, 100k.Pin_1, 4_7k.Pin_0, Battery.-
  N2: CPU.D10, CPU.D11/MOSI, CPU.D12/MISO, Auto_Switch.COM, Trigger_Switch.COM, Disconnector_Switch.COM, 4_7k.Pin_1
  N3: CPU.VIN, 1M.Pin_0, Battery.+
  N4: CPU.5V, Auto_Switch.L2, Trigger_Switch.L1, Disconnector_Switch.L1
  N5: CPU.A0, 100k.Pin_0, 1M.Pin_1
